// Logisim project Watson.circ as structural Verilog: 13 circuits, main circuit main
module main (
);

  wire alu_1_eq, and_1_out, clock_1_out, clock_2_out, clock_3_out, control_1_alusrc, control_1_cbr,
       control_1_memread, control_1_memtoreg, control_1_memwrite, control_1_regwrite, control_1_ubr,
       or_1_out, or_2_out, register_2_q;
  wire [2:0] control_1_aluop;
  wire [15:0] adder_16b_1_x, alu_1_aluout, bit_extender_1_out, dataram_dout, multiplexer_1_out,
       multiplexer_2_out, multiplexer_3_out, multiplexer_4_out, regfile_8x16b_1_readdata1,
       regfile_8x16b_1_readdata2, regfile_8x16b_1_readdata3, register_1_q, rom_1_data;

  Clock clock_1 (.out(clock_1_out));
  Register #(.width(16)) register_1 (
    .D(multiplexer_1_out), .en(clock_1_out), .clk(clock_1_out), .Q(register_1_q));  // open: clr
  adder_16b adder_16b_1 (.a(register_1_q), .cin(1'b0), .b(16'h1), .x(adder_16b_1_x));  // open: cout
  Multiplexer #(.width(16)) multiplexer_1 (
    .in0(adder_16b_1_x), .in1(alu_1_aluout), .out(multiplexer_1_out), .sel(or_2_out));
  ROM #(.addrWidth(16), .dataWidth(16)) rom_1 (.addr(register_1_q), .data(rom_1_data));
  control control_1 (
    .op(rom_1_data[14:12]), .md(rom_1_data[15]), .ALUop(control_1_aluop), .ALUsrc(control_1_alusrc),
    .UBr(control_1_ubr), .CBr(control_1_cbr), .MemToReg(control_1_memtoreg), .MemWrite(control_1_memwrite),
    .MemRead(control_1_memread), .RegWrite(control_1_regwrite));
  Clock clock_2 (.out(clock_2_out));
  RAM #(.addrWidth(16), .dataWidth(16)) dataram (
    .addr(alu_1_aluout), .we(control_1_memwrite), .oe(control_1_memread), .clk(clock_2_out),
    .din(regfile_8x16b_1_readdata3), .dout(dataram_dout));
  Multiplexer #(.width(16)) multiplexer_2 (
    .in0(alu_1_aluout), .in1(dataram_dout), .out(multiplexer_2_out), .sel(control_1_memtoreg));
  assign bit_extender_1_out = {{13{1'b0}}, rom_1_data[2:0]};  // Bit_Extender bit_extender_1
  regfile_8x16b regfile_8x16b_1 (
    .Enabled(1'b1), .WriteReg(rom_1_data[5:3]), .ReadReg1(rom_1_data[11:9]), .RegWrite(control_1_regwrite),
    .RegDataW(multiplexer_2_out), .ReadReg2(rom_1_data[8:6]), .ReadReg3(rom_1_data[5:3]),
    .ReadData1(regfile_8x16b_1_readdata1), .ReadData2(regfile_8x16b_1_readdata2),
    .ReadData3(regfile_8x16b_1_readdata3));
  Multiplexer #(.width(16)) multiplexer_3 (
    .in0(regfile_8x16b_1_readdata2), .in1(bit_extender_1_out), .out(multiplexer_3_out), .sel(control_1_alusrc));
  Multiplexer #(.width(16)) multiplexer_4 (
    .in0(regfile_8x16b_1_readdata1), .in1(register_1_q), .out(multiplexer_4_out), .sel(or_1_out));
  or or_1 (or_1_out, control_1_ubr, control_1_cbr);
  and and_1 (and_1_out, control_1_cbr, register_2_q);
  or or_2 (or_2_out, control_1_ubr, and_1_out);
  ALU alu_1 (
    .ALUop(control_1_aluop), .Data1(multiplexer_4_out), .Data2(multiplexer_3_out), .ALUout(alu_1_aluout),
    .EQ(alu_1_eq));
  Register #(.width(1)) register_2 (.D(alu_1_eq), .en(clock_3_out), .clk(clock_3_out), .Q(register_2_q));  // open: clr
  Clock clock_3 (.out(clock_3_out));

  // Notes on the sheet:
  //   Benicio Hernandez
  //   PC
  //   NextPC
  //   Watson - named after my cat :)
  //   I pledge my honor that I have abided by the Stevens Honor System.
  //   PC to ALU
  //   contents of rom_1 (hex, n*v repeats v):
  //   8002 820a 3050 8618 a610 5000
  //   Instruction memory
  //   WARN: Mux must choose nextPC by default!
  //   mod
  //   opcode
  //   WriteReg
  //   ReadReg2
  //   ReadReg1
  //   PC to ALU
  //   Branching control
  //   Branching Return
  //   ^ Address / Data from ALU
  //   imm
  //   Data memory
  //   ^ ReadData1 (to mem)
  //   Cond. Branch
  //   U. Branch
  //   <- RegD1 OR PC if CBr OR UBr
  //   EQ Reg
endmodule

module one_b_adder (
  input  cin,
  input  a,
  input  b,
  output x,
  output cout
);

  wire and_1_out, and_2_out, and_3_out, xor_1_out;

  xor xor_1 (xor_1_out, cin, a);
  and and_1 (and_1_out, cin, b);
  and and_2 (and_2_out, cin, a);
  and and_3 (and_3_out, a, b);
  xor xor_2 (x, xor_1_out, b);
  or or_1 (cout, and_1_out, and_2_out, and_3_out);
endmodule

module eight_b_adder (
  input  [7:0] b,
  input  [7:0] a,
  input  cin,
  output [7:0] x,
  output cout
);

  wire one_b_adder_1_cout, one_b_adder_2_cout, one_b_adder_3_cout, one_b_adder_4_cout, one_b_adder_5_cout,
       one_b_adder_6_cout, one_b_adder_7_cout;

  one_b_adder one_b_adder_1 (.cin(cin), .a(b[0]), .b(a[0]), .x(x[0]), .cout(one_b_adder_1_cout));
  one_b_adder one_b_adder_2 (.cin(one_b_adder_1_cout), .a(b[1]), .b(a[1]), .x(x[1]), .cout(one_b_adder_2_cout));
  one_b_adder one_b_adder_3 (.cin(one_b_adder_2_cout), .a(b[2]), .b(a[2]), .x(x[2]), .cout(one_b_adder_3_cout));
  one_b_adder one_b_adder_4 (.cin(one_b_adder_3_cout), .a(b[3]), .b(a[3]), .x(x[3]), .cout(one_b_adder_4_cout));
  one_b_adder one_b_adder_5 (.cin(one_b_adder_4_cout), .a(b[4]), .b(a[4]), .x(x[4]), .cout(one_b_adder_5_cout));
  one_b_adder one_b_adder_6 (.cin(one_b_adder_5_cout), .a(b[5]), .b(a[5]), .x(x[5]), .cout(one_b_adder_6_cout));
  one_b_adder one_b_adder_7 (.cin(one_b_adder_6_cout), .a(b[6]), .b(a[6]), .x(x[6]), .cout(one_b_adder_7_cout));
  one_b_adder one_b_adder_8 (.cin(one_b_adder_7_cout), .a(b[7]), .b(a[7]), .x(x[7]), .cout(cout));
endmodule

module adder_16b (
  input  [15:0] a,
  input  cin,
  input  [15:0] b,
  output [15:0] x,
  output cout
);

  wire eight_b_adder_1_cout;

  eight_b_adder eight_b_adder_1 (.b(b[7:0]), .a(a[7:0]), .cin(cin), .x(x[7:0]), .cout(eight_b_adder_1_cout));
  eight_b_adder eight_b_adder_2 (.b(b[15:8]), .a(a[15:8]), .cin(eight_b_adder_1_cout), .x(x[15:8]), .cout(cout));
endmodule

module regfile_8x16b (
  input  Enabled,
  input  [2:0] WriteReg,
  input  [2:0] ReadReg1,
  input  RegWrite,
  input  [15:0] RegDataW,
  input  [2:0] ReadReg2,
  input  [2:0] ReadReg3,
  output [15:0] ReadData1,
  output [15:0] ReadData2,
  output [15:0] ReadData3
);

  wire and_1_out, and_2_out, and_3_out, and_4_out, and_5_out, and_6_out, and_7_out, and_8_out, clock_1_out,
       decoder_1_out0, decoder_1_out1, decoder_1_out2, decoder_1_out3, decoder_1_out4, decoder_1_out5,
       decoder_1_out6, decoder_1_out7;
  wire [15:0] X1_q, X2_q, X3_q, X4_q, X5_q, X6_q, X7_q, X8_q;

  Decoder #(.select(3)) decoder_1 (
    .out0(decoder_1_out0), .out1(decoder_1_out1), .out2(decoder_1_out2), .out3(decoder_1_out3),
    .out4(decoder_1_out4), .out5(decoder_1_out5), .out6(decoder_1_out6), .out7(decoder_1_out7),
    .sel(WriteReg), .en(Enabled));
  Register #(.width(16)) X1 (.D(RegDataW), .en(and_1_out), .clk(clock_1_out), .Q(X1_q));  // open: clr
  Clock clock_1 (.out(clock_1_out));
  and and_1 (and_1_out, decoder_1_out0, RegWrite);
  Register #(.width(16)) X2 (.D(RegDataW), .en(and_2_out), .clk(clock_1_out), .Q(X2_q));  // open: clr
  and and_2 (and_2_out, decoder_1_out1, RegWrite);
  Register #(.width(16)) X3 (.D(RegDataW), .en(and_3_out), .clk(clock_1_out), .Q(X3_q));  // open: clr
  and and_3 (and_3_out, decoder_1_out2, RegWrite);
  Register #(.width(16)) X4 (.D(RegDataW), .en(and_4_out), .clk(clock_1_out), .Q(X4_q));  // open: clr
  and and_4 (and_4_out, decoder_1_out3, RegWrite);
  Register #(.width(16)) X5 (.D(RegDataW), .en(and_5_out), .clk(clock_1_out), .Q(X5_q));  // open: clr
  and and_5 (and_5_out, decoder_1_out4, RegWrite);
  Register #(.width(16)) X6 (.D(RegDataW), .en(and_6_out), .clk(clock_1_out), .Q(X6_q));  // open: clr
  and and_6 (and_6_out, decoder_1_out5, RegWrite);
  Register #(.width(16)) X7 (.D(RegDataW), .en(and_7_out), .clk(clock_1_out), .Q(X7_q));  // open: clr
  and and_7 (and_7_out, decoder_1_out6, RegWrite);
  Register #(.width(16)) X8 (.D(RegDataW), .en(and_8_out), .clk(clock_1_out), .Q(X8_q));  // open: clr
  and and_8 (and_8_out, decoder_1_out7, RegWrite);
  Multiplexer #(.select(3), .width(16)) multiplexer_1 (
    .in0(X1_q), .in1(X2_q), .in2(X3_q), .in3(X4_q), .in4(X5_q), .in5(X6_q), .in6(X7_q), .in7(X8_q),
    .out(ReadData1), .sel(ReadReg1));
  Multiplexer #(.select(3), .width(16)) multiplexer_2 (
    .in0(X1_q), .in1(X2_q), .in2(X3_q), .in3(X4_q), .in4(X5_q), .in5(X6_q), .in6(X7_q), .in7(X8_q),
    .out(ReadData2), .sel(ReadReg2));
  Multiplexer #(.select(3), .width(16)) multiplexer_3 (
    .in0(X1_q), .in1(X2_q), .in2(X3_q), .in3(X4_q), .in4(X5_q), .in5(X6_q), .in6(X7_q), .in7(X8_q),
    .out(ReadData3), .sel(ReadReg3));

  // Notes on the sheet:
  //   WriteReg
  //   RegDataW
endmodule

module ALU (
  input  [2:0] ALUop,
  input  [15:0] Data1,
  input  [15:0] Data2,
  output [15:0] ALUout,
  output EQ
);

  wire [15:0] adder_16b_1_x, sub_16b_1_x;

  adder_16b adder_16b_1 (.a(Data1), .cin(1'b0), .b(Data2), .x(adder_16b_1_x));  // open: cout
  sub_16b sub_16b_1 (.B(Data2), .A(Data1), .Bin(1'b0), .X(sub_16b_1_x));  // open: Bout
  comparator_16b comparator_16b_1 (.A(Data1), .B(Data2), .EQ(EQ));
  Multiplexer #(.select(3), .width(16)) multiplexer_1 (
    .in0(Data2), .in1(adder_16b_1_x), .in2(sub_16b_1_x), .in3({16{1'b0}}), .out(ALUout), .sel(ALUop));  // open: in4, in5, in6, in7

  // Notes on the sheet:
  //   ADD
  //   SUB
  //   CMP
  //   passthrough
endmodule

module control (
  input  [2:0] op,
  input  md,
  output [2:0] ALUop,
  output ALUsrc,
  output UBr,
  output CBr,
  output MemToReg,
  output MemWrite,
  output MemRead,
  output RegWrite
);

  wire [2:0] multiplexer_1_out, multiplexer_2_out;

  Multiplexer #(.width(3)) multiplexer_1 (.in0(3'b001), .in1(3'b010), .out(multiplexer_1_out), .sel(md));
  Multiplexer #(.width(3)) multiplexer_2 (.in0(3'b001), .in1(3'b010), .out(multiplexer_2_out), .sel(md));
  Multiplexer #(.select(3), .width(10)) multiplexer_3 (
    .in0({6'b100000, md, 3'b000}), .in1({6'b110100, md, 3'b001}), .in2({6'b001000, md, 3'b001}),
    .in3({6'b100000, md, 3'b001}), .in4({6'b100000, md, 3'b010}), .in5({7'b0000011, multiplexer_1_out}),
    .in6({7'b0000101, multiplexer_2_out}), .in7({{6{1'b0}}, md, 3'b011}),
    .out({RegWrite, MemRead, MemWrite, MemToReg, CBr, UBr, ALUsrc, ALUop}), .sel(op));

  // Notes on the sheet:
  //   mod 0 = add, 1 = sub
  //   change  ALUop based on mod
  //   changes direction of branch
  //   MOV
  //   LDR
  //   STR
  //   ADD
  //   SUB
  //   B
  //   BEQ
  //   CMP
endmodule

module sub_1b (
  input  A,
  input  B,
  input  Bin,
  output X,
  output Bout
);

  wire and_1_out, and_2_out, not_1_out, not_2_out, xor_1_out;

  not not_1 (not_1_out, B);
  xor xor_1 (xor_1_out, B, Bin);
  and and_1 (and_1_out, not_1_out, Bin);
  not not_2 (not_2_out, xor_1_out);
  xor xor_2 (X, A, xor_1_out);
  and and_2 (and_2_out, not_2_out, A);
  or or_1 (Bout, and_2_out, and_1_out);
endmodule

module sub_16b (
  input  [15:0] B,
  input  [15:0] A,
  input  Bin,
  output [15:0] X,
  output Bout
);

  wire sub_4b_1_bout, sub_4b_2_bout, sub_4b_3_bout;

  sub_4b sub_4b_1 (.B(B[3:0]), .A(A[3:0]), .Bin(Bin), .X(X[3:0]), .Bout(sub_4b_1_bout));
  sub_4b sub_4b_2 (.B(B[7:4]), .A(A[7:4]), .Bin(sub_4b_1_bout), .X(X[7:4]), .Bout(sub_4b_2_bout));
  sub_4b sub_4b_3 (.B(B[11:8]), .A(A[11:8]), .Bin(sub_4b_2_bout), .X(X[11:8]), .Bout(sub_4b_3_bout));
  sub_4b sub_4b_4 (.B(B[15:12]), .A(A[15:12]), .Bin(sub_4b_3_bout), .X(X[15:12]), .Bout(Bout));
endmodule

module sub_4b (
  input  [3:0] B,
  input  [3:0] A,
  input  Bin,
  output [3:0] X,
  output Bout
);

  wire sub_1b_1_bout, sub_1b_2_bout, sub_1b_3_bout;

  sub_1b sub_1b_1 (.A(B[0]), .B(A[0]), .Bin(Bin), .X(X[0]), .Bout(sub_1b_1_bout));
  sub_1b sub_1b_2 (.A(B[1]), .B(A[1]), .Bin(sub_1b_1_bout), .X(X[1]), .Bout(sub_1b_2_bout));
  sub_1b sub_1b_3 (.A(B[2]), .B(A[2]), .Bin(sub_1b_2_bout), .X(X[2]), .Bout(sub_1b_3_bout));
  sub_1b sub_1b_4 (.A(B[3]), .B(A[3]), .Bin(sub_1b_3_bout), .X(X[3]), .Bout(Bout));
endmodule

module comparator_16b (
  input  [15:0] A,
  input  [15:0] B,
  output EQ
);

  wire comparator_4b_1_eq, comparator_4b_2_eq, comparator_4b_3_eq, comparator_4b_4_eq;

  comparator_4b comparator_4b_1 (.A(A[3:0]), .B(B[3:0]), .EQ(comparator_4b_1_eq));
  comparator_4b comparator_4b_2 (.A(A[7:4]), .B(B[7:4]), .EQ(comparator_4b_2_eq));
  comparator_4b comparator_4b_3 (.A(A[11:8]), .B(B[11:8]), .EQ(comparator_4b_3_eq));
  comparator_4b comparator_4b_4 (.A(A[15:12]), .B(B[15:12]), .EQ(comparator_4b_4_eq));
  and and_1 (EQ, comparator_4b_1_eq, comparator_4b_2_eq, comparator_4b_3_eq, comparator_4b_4_eq);
endmodule

module comparator_1b (
  input  A,
  input  B,
  output EQ
);

  wire and_1_out, and_2_out, not_1_out, not_2_out;

  not not_1 (not_1_out, A);
  not not_2 (not_2_out, B);
  and and_1 (and_1_out, not_1_out, B);
  and and_2 (and_2_out, A, not_2_out);
  nor nor_1 (EQ, and_1_out, and_2_out);
endmodule

module comparator_4b (
  input  [3:0] A,
  input  [3:0] B,
  output EQ
);

  wire comparator_1b_1_eq, comparator_1b_2_eq, comparator_1b_3_eq, comparator_1b_4_eq;

  comparator_1b comparator_1b_1 (.A(A[0]), .B(B[0]), .EQ(comparator_1b_1_eq));
  comparator_1b comparator_1b_2 (.A(A[1]), .B(B[1]), .EQ(comparator_1b_2_eq));
  comparator_1b comparator_1b_3 (.A(A[2]), .B(B[2]), .EQ(comparator_1b_3_eq));
  comparator_1b comparator_1b_4 (.A(A[3]), .B(B[3]), .EQ(comparator_1b_4_eq));
  and and_1 (EQ, comparator_1b_1_eq, comparator_1b_2_eq, comparator_1b_3_eq, comparator_1b_4_eq);
endmodule
